# Fritzing sketch Ultrasonic.robot (saved by Fritzing 0.9.3b)
breadboards: 1

parts:
  Part1 = Arduino Uno (Rev3)
  J1 = Piezo Speaker
  hc-sr1 = hc-sr04
  Part2 = LED Matrix - Serial Interface - Red/Green/Blue
  Part3 = LED Matrix - Serial Interface - Red/Green/Blue
  LED1 = RGB LED (com. cathode, rgb) [package="5 mm [THT]"]
  LED2 = RGB LED (com. cathode, rgb) [package="5 mm [THT]"]
  LED3 = RGB LED (com. cathode, rgb) [package="5 mm [THT]"]
  R2 = Resistor [tolerance=±5% resistance=220 package="1206 [SMD]"]
  R3 = Resistor [tolerance=±5% resistance=220 package="1206 [SMD]"]
  R4 = Resistor [tolerance=±5% resistance=220 package="1206 [SMD]"]
  R5 = Resistor [tolerance=±5% resistance=220 package="1206 [SMD]"]
  R6 = Resistor [tolerance=±5% resistance=220 package="1206 [SMD]"]
  R7 = Resistor [tolerance=±5% resistance=220 package="1206 [SMD]"]

nets:
  VCC: Part1.A4/SDA, Part1.5V, J1.pin2, hc-sr1.VCC, Part2.VCC, Part2.SCK, Part3.VCC
  N1: Part1.A5/SCL, Part2.CS
  N2: Part1.D9_PWM, R2.Pin_1
  N3: Part1.D11_PWM/MOSI, hc-sr1.Echo
  N4: Part1.D12/MISO, Part3.MISO
  N5: Part1.D13/SCK, R3.Pin_1
  N6: Part1.D1/TX, R7.Pin_1
  N7: Part1.D2, R6.Pin_1
  N8: Part1.D3_PWM, Part2.MISO
  N9: Part1.D4, Part3.CS
  N10: Part1.D6_PWM, hc-sr1.Trig
  N11: Part1.D7, R5.Pin_1
  GND: Part1.GND, J1.pin1, hc-sr1.GND, Part2.GND, Part3.GND, LED1.common_cathode, LED2.common_cathode, LED3.common_cathode
  N12: LED1.red_anode, R3.Pin_0
  N13: LED1.green_anode, R2.Pin_0
  N14: LED2.red_anode, R4.Pin_0
  N15: LED2.green_anode, R5.Pin_0
  N16: LED3.red_anode, R6.Pin_0
  N17: LED3.green_anode, R7.Pin_0

notes:
  All of the pins along the blue/violet line are connected to GND
  All of the pins along the red line are connected to 5V
