# Fritzing sketch Untitled Sketch 2 (saved by Fritzing 0.9.3b)
breadboards: 1

parts:
  Part1 = Arduino Uno (Rev3)
  Part2 = LED Matrix - Serial Interface - Red/Green/Blue
  Part3 = LED Matrix - Serial Interface - Red/Green/Blue
  LED1 = RGB LED (com. anode, rbg) [package="5 mm [THT]"]
  LED2 = RGB LED (com. anode, rbg) [package="5 mm [THT]"]
  J1 = Piezo Speaker  # not connected
  hc-sr1 = hc-sr04  # not connected
  R1 = Resistor [tolerance=±5% resistance=220 package=THT]
  R2 = Resistor [tolerance=±5% resistance=220 package=THT]

nets:
  N1: Part1.D8, LED1.green_cathode
  N2: Part1.GND, Part2.CS, Part3.CS
  N3: Part1.5V, Part2.SCK, Part3.SCK, R1.Pin_0, R2.Pin_0
  N4: LED1.common_anode, R1.Pin_1
  N5: LED2.common_anode, R2.Pin_1

notes:
  Our LED Matrices have I2C backpacks attached, so they are slightly different in sizing and wiring (there are no backpacks in fritzing).
