# Fritzing sketch final.fritzing (saved by Fritzing 0.9.3b)
breadboards: 1

parts:
  Part1 = Arduino Uno (Rev3)
  Part2 = LED Matrix - Serial Interface - Red/Green/Blue
  Part3 = LED Matrix - Serial Interface - Red/Green/Blue
  LED1 = RGB LED (com. anode, rbg) [package="5 mm [THT]"]
  LED2 = RGB LED (com. anode, rbg) [package="5 mm [THT]"]
  J1 = Piezo Speaker
  hc-sr1 = hc-sr04
  R1 = Resistor [tolerance=±5% resistance=220 package=THT]
  R2 = Resistor [tolerance=±5% resistance=220 package=THT]

nets:
  N1: Part1.A4/SDA, Part2.MOSI, Part3.MOSI
  GND: Part1.A5/SCL, Part2.GND, Part3.GND
  N2: Part1.D8, LED1.green_cathode
  N3: Part1.D9_PWM, J1.pin1
  N4: Part1.D10_PWM/SS, LED2.red_cathode
  N5: Part1.D11_PWM/MOSI, LED2.green_cathode
  N6: Part1.D12/MISO, LED1.red_cathode
  GND_2: Part1.GND, Part2.CS, Part3.CS, hc-sr1.GND
  N7: Part1.D2, hc-sr1.Echo
  N8: Part1.D6_PWM, hc-sr1.Trig
  5V: Part1.5V, Part2.SCK, Part3.SCK, J1.pin2, hc-sr1.VCC, R1.Pin_0, R2.Pin_0
  N9: LED1.common_anode, R1.Pin_1
  N10: LED2.common_anode, R2.Pin_1

notes:
  Our LED Matrices have I2C backpacks attached, so they are slightly different in sizing and wiring (there are no backpacks in fritzing).
